# Fritzing sketch Hauptschaltplan (saved by Fritzing 1.0.6)

parts:
  A1 = Arduino UNO R4 WiFi
  A2 = drv-1012
  M2 = E18-D80NK_1 [package=THT]
  M3 = DC Motor [voltage_(max)=6V voltage_(min)=3V]
  V1 = DC Power Supply [voltage=12V internal_resistance=1Ω max_current=0.1A]
  R1 = Rotary Potentiometer (Small) [maximum_resistance=10kΩ knob_status=50% power=0.5W package=THT]
  M1 = E18-D80NK_1 [package=THT]
  C1 = Electrolytic Capacitor [capacitance=1µF voltage=35V package="100 mil [THT, electrolytic]"]
  LCD2004-I2C1 = LCD2004-I2C  # not connected
  R2 = Resistor [tolerance=±5% power=0.25W resistance=10000 package=THT]  # not connected
  C2 = Electrolytic Capacitor [capacitance=1µF voltage=35V package="100 mil [THT, electrolytic]"]  # not connected
  S1 = Momentary Switch 6mm 2pin  # not connected
  S2 = Momentary Switch 6mm 2pin  # not connected
  S3 = Taiway 100-SP-X-T1 SPDT Miniature Toggle Switch [part_number=100-SP-X-T1-0-0-B1-M1 package=THT]  # not connected

nets (from the breadboard view):
  N1: A1.Pin_2, A1.Pin_9, A1.Pin_10, A1.Pin_25, A1.Pin_30, A2.Pin_1, M2.pin1, R1.leg2, M1.pin1, C1.-
  N2: A1.Pin_8, A1.Pin_27, A2.Pin_3, A2.Pin_7, M2.pin2, R1.leg1, M1.pin2
  N3: A1.Pin_11, A2.Pin_5, C1.+
  N4: A1.Pin_12, R1.wiper
  N5: A1.Pin_36, M1.pin3
  N6: A1.Pin_38, M2.pin3
  N7: A1.Pin_39, A2.Pin_4
  N8: A1.Pin_40, A2.Pin_8
  N9: A2.Pin_9, M3.pin_2
  N10: A2.Pin_10, M3.pin_1
  N11: A2.Pin_11, V1.Pin_2
  N12: A2.Pin_12, V1.Pin_1

custom parts:
  Arduino UNO R4 WiFi: The Arduino UNO R4 WiFi merges the RA4M1 microprocessor from Renesas with the ESP32-S3 from Espressif, creating an all-in-one tool for makers with enhanced processing power and a diverse array of new peripherals.
  drv-1012: .The BTS7960 is a fully integrated high current H bridge module for motor drive applications.
  E18-D80NK_1: E18-D80NK Proximity Sensor module.
  LCD2004-I2C: A standard character display with 4x20 characters. Comes in many colors with LCM2004 IIC attached.
  Momentary Switch 6mm 2pin: Momentary Switch 6mm 2 pin Button commonly used for reset or general input.
